# Fritzing sketch U2D2 통신 회로 (saved by Fritzing 0.9.4)
perfboards: 1

parts:
  R2 = Resistor [tolerance=±5% resistance=10k package=THT]  # not connected
  U6 = 74HC126N [package=dil14]
  U7 = 74HC04AP [package=dil14]

nets:
  N1: U6.1A, U7.1Y

notes:
  5V
  TXD
  GND
  DATA
  DIR
  RXD
